// Logisim project p1.circ as structural Verilog: 7 circuits, main circuit main
module main (
  input  [7:0] Ctrl,
  input  [7:0] i00,
  input  [7:0] i01,
  input  [7:0] i10,
  input  [7:0] i11,
  input  [7:0] Addr,
  input  [7:0] Data,
  input  Enable,
  output [7:0] o00,
  output [7:0] o01,
  output [7:0] o10,
  output [7:0] o11,
  output [7:0] Ctrl_Cur,
  output [7:0] Addr_Cur,
  output [7:0] Data_Cur
);

  wire Clk_out;

  Clock Clk (.out(Clk_out));
  CPU cpu_1 (
    .Control(Ctrl), .Address(Addr), .Data_Wr(Data), .Enable(Enable), .Control_Out(Ctrl_Cur),
    .Address_Out(Addr_Cur), .Wr_Out(Data_Cur));  // open: Data_Read, Rd_Out
  mem_unit mem_unit_1 (
    .Data_In(Data_Cur), .Address(Addr_Cur), .Control(Ctrl_Cur), .Enable(Enable), .Clk(Clk_out),
    .Data_Out(Data_Cur));
  IO_Sys IO (
    .Data_In(Data_Cur), .Clk(Clk_out), .i00(i00), .i01(i01), .i10(i10), .i11(i11), .Address(Addr_Cur),
    .Control(Ctrl_Cur), .Enable(Enable), .o00(o00), .o01(o01), .o10(o10), .o11(o11), .Data_Out(Data_Cur));  // open: R

  // Notes on the sheet:
  //   Small Control Guide:
  //   MEMORY R/W
  //   xx01: (MEM) READ
  //   xx00: (MEM) WR
  //   10xx: RAM
  //   01xx: ROM
  //   +Addr = 8-bit Address
  //   Control
  //   Address
  //   Data
  //   Both: +Data = To-WR
  //   IO R/W
  //   xx11: (IO) READ
  //   xx00: (IO) WR
  //   +Addr = IO Device
endmodule

module tri_buffer (
  input  c,
  input  [7:0] i,
  output [7:0] o
);

  wire not_1_out;

  not not_1 (not_1_out, c);
  Transistor #(.width(8)) transistor_1 (.in(i), .out(o), .gate(not_1_out));
  Transistor #(.\type ("n"), .width(8)) transistor_2 (.in(i), .out(o), .gate(c));

  // Notes on the sheet:
  //   8-bit tri state buffer
endmodule

module CPU (
  input  [7:0] Control,
  input  [7:0] Address,
  input  [7:0] Data_Wr,
  input  [7:0] Data_Read,
  input  Enable,
  output [7:0] Control_Out,
  output [7:0] Address_Out,
  output [7:0] Wr_Out,
  output [7:0] Rd_Out
);

  wire [7:0] rd_wr_buffer_1_data_out;

  tri_buffer tri_buffer_1 (.i(Control), .c(Enable), .o(Control_Out));
  tri_buffer tri_buffer_2 (.i(Address), .c(Enable), .o(Address_Out));
  rd_wr_buffer rd_wr_buffer_1 (.Data_In(Data_Wr), .Control(Control), .Data_Out(rd_wr_buffer_1_data_out));
  tri_buffer tri_buffer_3 (.i(rd_wr_buffer_1_data_out), .c(Enable), .o(Wr_Out));
  tri_buffer tri_buffer_4 (.i(Data_Read), .c(Enable), .o(Rd_Out));

  // Notes on the sheet:
  //   CPU writes to Data on RD
endmodule

module IO_Sys (
  input  [7:0] i00,
  input  [7:0] i01,
  input  [7:0] i10,
  input  Clk,
  input  R,
  input  [7:0] i11,
  input  [7:0] Data_In,
  input  Enable,
  input  [7:0] Control,
  input  [7:0] Address,
  output [7:0] o00,
  output [7:0] o01,
  output [7:0] o10,
  output [7:0] o11,
  output [7:0] Data_Out
);

  wire decoder_1_out0, decoder_1_out1, decoder_1_out2, decoder_1_out3, io_rd_out, io_wr_out, not_1_out;
  wire [7:0] multiplexer_2_out, multiplexer_3_out, tri_buffer_1_o;

  // NoConnect on Address[7:2]
  and io_rd (io_rd_out, Control[0], Enable, Control[1]);
  and io_wr (io_wr_out, Control[1], Enable, not_1_out);
  not not_1 (not_1_out, Control[0]);
  Decoder #(.select(2)) decoder_1 (
    .out0(decoder_1_out0), .out1(decoder_1_out1), .out2(decoder_1_out2), .out3(decoder_1_out3),
    .sel(Address[1:0]), .en(io_wr_out));
  Register register_1 (.D(Data_In), .en(decoder_1_out0), .clk(Clk), .Q(o00), .clr(R));
  Register register_2 (.D(Data_In), .en(decoder_1_out1), .clk(Clk), .Q(o01), .clr(R));
  Register register_3 (.D(Data_In), .en(decoder_1_out2), .clk(Clk), .Q(o10), .clr(R));
  Register register_4 (.D(Data_In), .en(decoder_1_out3), .clk(Clk), .Q(o11), .clr(R));
  Multiplexer #(.width(8)) multiplexer_1 (.in0(tri_buffer_1_o), .out(Data_Out), .sel(io_wr_out));  // open: in1
  // NoConnect on multiplexer_2_out
  Multiplexer #(.select(2), .width(8)) multiplexer_2 (
    .in0(o00), .in1(o01), .in2(o10), .in3(o11), .out(multiplexer_2_out), .sel(Address[1:0]));
  Multiplexer #(.select(2), .width(8)) multiplexer_3 (
    .in0(i00), .in1(i01), .in2(i10), .in3(i11), .out(multiplexer_3_out), .sel(Address[1:0]));
  tri_buffer tri_buffer_1 (.i(multiplexer_3_out), .c(io_rd_out), .o(tri_buffer_1_o));

  // Notes on the sheet:
  //   ^Disconnected Here
endmodule

module mem_unit (
  input  [7:0] Data_In,
  input  [7:0] Address,
  input  [7:0] Control,
  input  Enable,
  input  Clk,
  output [7:0] Data_Out
);

  wire C_out, C_RAM_out, C_ROM_out, not_1_out, not_2_out;
  wire [7:0] ram_1_dout, rom_1_data;

  // NoConnect on Control[7:4]
  ROM rom_1 (.addr(Address), .data(rom_1_data));
  not not_1 (not_1_out, Control[1]);
  and C (C_out, not_1_out, Enable);
  // NoConnect on not_1_out
  // NoConnect on Control[2]
  // NoConnect on Control[3]
  tri_buffer tri_buffer_1 (.i(rom_1_data), .c(C_ROM_out), .o(Data_Out));
  and C_RAM (C_RAM_out, Control[3], Control[0], C_out);
  and C_ROM (C_ROM_out, C_out, Control[2]);
  RAM ram_1 (.addr(Address), .we(not_2_out), .oe(Control[0]), .clk(Clk), .din(Data_In), .dout(ram_1_dout));
  not not_2 (not_2_out, Control[0]);
  tri_buffer tri_buffer_2 (.i(ram_1_dout), .c(C_RAM_out), .o(Data_Out));

  // Notes on the sheet:
  //   0: 0/1 = WR/RD
  //   1: IO/M-low
  //   2: C_ROM
  //   3: C_RAM
  //   contents of rom_1 (hex, n*v repeats v):
  //   0 1 2 3 4 5 6 7 8 9 10 11 12 13 14 15
  //   only used by ram
  //   WR (0), RD (1)
  //   RAM Control
  //   ROM Control
  //   Clk
  //   invalid read until first clk (unspecified ptr)
endmodule

module rd_wr_buffer (
  input  [7:0] Data_In,
  input  [7:0] Control,
  output [7:0] Data_Out
);

  wire not_1_out;

  // NoConnect on Control[7:1]
  not not_1 (not_1_out, Control[0]);
  tri_buffer tri_buffer_1 (.i(Data_In), .c(not_1_out), .o(Data_Out));

  // Notes on the sheet:
  //   CTRL Bit 0 :: 0/1 = WR/RD
  //   just crops 8-bit control into rd/wr based buffer
endmodule

module tri_buffer1b (
  input  c,
  input  i,
  output o
);

  wire not_1_out;

  not not_1 (not_1_out, c);
  Transistor transistor_1 (.in(i), .out(o), .gate(not_1_out));
  Transistor #(.\type ("n")) transistor_2 (.in(i), .out(o), .gate(c));

  // Notes on the sheet:
  //   1-bit tri-state buffer
endmodule
